// Logisim project Calculadora Digital.circ as structural Verilog
module somador (
  input  A1,
  input  A2,
  input  A3,
  input  B1,
  input  B2,
  input  B3,
  input  A0,
  input  B0,
  output Carry,
  output S0,
  output S1,
  output S2,
  output S3
);

  wire meio_somador_carry, somador_completo_2_carry, somador_completo_carry;

  meio_somador meio_somador (.A(A0), .B(B0), .Soma(S0), .Carry(meio_somador_carry));
  somador_completo somador_completo (
    .A(A1), .B(B1), .Cin(meio_somador_carry), .Soma(S1), .Carry(somador_completo_carry));
  somador_completo somador_completo_2 (
    .A(A2), .B(B2), .Cin(somador_completo_carry), .Soma(S2), .Carry(somador_completo_2_carry));
  somador_completo somador_completo_3 (.A(A3), .B(B3), .Cin(somador_completo_2_carry), .Soma(S3), .Carry(Carry));
endmodule

module multiplexador (
  input  in_1,
  input  in_2
);
endmodule

module meio_somador (
  input  A,
  input  B,
  output Soma,
  output Carry
);

  xor xor_1 (Soma, A, B);
  and and_1 (Carry, A, B);
endmodule

module subtrator (
  input  A1,
  input  A2,
  input  A3,
  input  B1,
  input  B2,
  input  B3,
  input  A0,
  input  B0,
  output Carry,
  output S0,
  output S1,
  output S2,
  output S3
);

  wire not_1_out, not_2_out, not_3_out, not_4_out, somador_completo_1_carry, somador_completo_2_carry,
       somador_completo_3_carry;

  somador_completo somador_completo_1 (.A(A0), .B(not_1_out), .Cin(1'b1), .Soma(S0), .Carry(somador_completo_1_carry));
  not not_1 (not_1_out, B0);
  somador_completo somador_completo_2 (
    .A(A1), .B(not_2_out), .Cin(somador_completo_1_carry), .Soma(S1), .Carry(somador_completo_2_carry));
  not not_2 (not_2_out, B1);
  not not_3 (not_3_out, B2);
  somador_completo somador_completo_3 (
    .A(A2), .B(not_3_out), .Cin(somador_completo_2_carry), .Soma(S2), .Carry(somador_completo_3_carry));
  somador_completo somador_completo_4 (.A(A3), .B(not_4_out), .Cin(somador_completo_3_carry), .Soma(S3), .Carry(Carry));
  not not_4 (not_4_out, B3);
endmodule

module complemento_de_2 (
  input  B0,
  input  B1,
  input  B2,
  input  B3,
  output out_5,
  output out_6,
  output out_7,
  output out_8
);

  // NOT_Gate not_1 has open pins: in=B0, out=open
  // NOT_Gate not_2 has open pins: in=B1, out=open
  // NOT_Gate not_3 has open pins: in=B2, out=open
  // NOT_Gate not_4 has open pins: in=B3, out=open
  meio_somador meio_somador_1 ();  // open: A, B, Soma, Carry
endmodule

module somador_completo (
  input  A,
  input  B,
  input  Cin,
  output Soma,
  output Carry
);

  wire and_1_out, and_2_out, xor_1_out;

  xor xor_1 (xor_1_out, A, B);
  xor xor_2 (Soma, Cin, xor_1_out);
  and and_1 (and_1_out, xor_1_out, Cin);
  and and_2 (and_2_out, A, B);
  or or_1 (Carry, and_1_out, and_2_out);
endmodule
